// Logisim project add-1.circ as structural Verilog: 2 circuits, main circuit main
module main (
  input  A,
  input  B,
  input  A_2,
  input  B_2,
  input  C,
  input  C_2,
  output V,
  output out_8,
  output S,
  output out_10
);

  wire and_1_out, and_2_out, or_1_out, xor_1_out;

  add_1 add_1_1 (.out_4(V), .out_5(S), .A(A), .B(B), .C(C_2));
  xor xor_1 (xor_1_out, A_2, B_2);
  or or_1 (or_1_out, C, B_2);
  and and_1 (and_1_out, C, B_2);
  and and_2 (and_2_out, or_1_out, A_2);
  xor xor_2 (out_8, xor_1_out, C);
  or or_2 (out_10, and_2_out, and_1_out);

  // Notes on the sheet:
  //   {
  //   MACRO:
  //   S = (A + B) + C
  //   V = A . (B + C) + (B . C)
  //   °
  //   °
  //   MICRO:
endmodule

module add_1 (
  input  A,
  input  B,
  input  C,
  output out_4,
  output out_5
);

  wire and_1_out, and_2_out, or_1_out, xor_1_out;

  and and_1 (and_1_out, C, B);
  xor xor_1 (xor_1_out, A, B);
  or or_1 (or_1_out, C, B);
  xor xor_2 (out_4, xor_1_out, C);
  and and_2 (and_2_out, or_1_out, A);
  or or_2 (out_5, and_2_out, and_1_out);
endmodule
